# Fritzing sketch gps-backtrack (saved by Fritzing 0.9.3b)
stripboards: 1

parts:
  Part1 = adafruit [part_number="Adafruit #2000"]
  B1 = Momentary Switch [package=ksa_sealed_tac_switch]
  B2 = Momentary Switch [package=ksa_sealed_tac_switch]
  S2 = Toggle Switch [package=THT]
  S1 = Toggle Switch [package=THT]
  OLED_I2C1 = OLED 128x64 I2C Monochrome Display
  U1 = SUP500F [package=sup500f]
  VCC1 = Battery

nets:
  GND: Part1.connector72, B1.1, B1.2, B2.1, B2.2, OLED_I2C1.GND, U1.GND, VCC1.-
  VDD: Part1.connector74, S2.L2, OLED_I2C1.VDD, U1.VCC
  N1: Part1.connector78, B2.3, B2.4
  N2: Part1.connector79, B1.3, B1.4
  N3: Part1.connector81, S1.L2
  N4: Part1.connector95, OLED_I2C1.SDA
  N5: Part1.connector96, OLED_I2C1.SCK
  N6: S2.COM, VCC1.+
  N7: S1.COM, U1.TX-O

notes:
  purple: OLED SCL <-> Pro SCL
  orange: OLED SDA <-> Pro SDA
  blue: screen btn <-> Pro 3
  yellow: save btn <-> Pro 4
  white: GPS TX <-> Pro RX (switched)
  B1: Display screen selection button
  B2: Save current coords button
  S1: Programming mode (off position, detaches serial interface)
  S2: Master power on/off
